# Fritzing sketch tapecleaner (saved by Fritzing 0.9.0b)

parts:
  Arduino2 = Arduino Uno (Rev3)
  M1 = DC Motor
  Part1 = Arduino Motor Shield (Rev3)
  M2 = DC Motor
  U1 = LCD-16X2 [package=lcd-8x2]  # not connected

nets:
  N1: Arduino2.A0, Part1.A0
  N2: Arduino2.A1, Part1.A1
  N3: Arduino2.A2, Part1.A2
  N4: Arduino2.A3, Part1.A3
  N5: Arduino2.A4/SDA, Part1.A4, Part1.SDA
  N6: Arduino2.A5/SCL, Part1.A5, Part1.SCL
  N7: Arduino2.D8, Part1.D8/BreakeB
  N8: Arduino2.D9_PWM, Part1.D9/BreakeA
  N9: Arduino2.D10_PWM/SS, Part1.D10_PWM
  N10: Arduino2.D11_PWM/MOSI, Part1.D11_PWM/B
  N11: Arduino2.D12/MISO, Part1.D12/DirA
  N12: Arduino2.D13/SCK, Part1.D13/DirB
  GND: Arduino2.GND, Part1.GND
  N13: Arduino2.AREF, Part1.AREF
  N14: Arduino2.D0/RX, Part1.IOREF#118
  N15: Arduino2.D1/TX, Part1.D1/TX
  N16: Arduino2.D2, Part1.D2
  N17: Arduino2.D3_PWM, Part1.D3_PWM/A
  N18: Arduino2.D4, Part1.D4
  N19: Arduino2.D5_PWM, Part1.D5_PWM
  N20: Arduino2.D6_PWM, Part1.D6_PWM
  N21: Arduino2.D7, Part1.D7
  N22: Arduino2.ioref, Part1.IOREF#147
  N23: Arduino2.RESET, Part1.RESET
  3V3: Arduino2.3V3, Part1.3V3
  5V: Arduino2.5V, Part1.5V
  VIN: Arduino2.VIN, Part1.VIN
  N24: M1.pin_1, Part1.A+
  N25: M1.pin_2, Part1.A-
  N26: Part1.B-, M2.pin_2
  N27: Part1.B+, M2.pin_1
